// Logisim project CORDIC-BASSO-FELIPE-E-LUCAS.circ as structural Verilog: 9 circuits, main circuit main
module main (
  input  [7:0] data,
  output [3:0] next_state,
  output DONE,
  output [31:0] sin,
  output [31:0] cos
);

  wire clk_out, cordic_1_en, data_av_out, Reset_out, start_out, sync_bt_out;
  wire [4:0] cordic_1_adres;
  wire [31:0] register_1_q, rom_1_data;

  Button_part data_av (.out(data_av_out));
  // Probe on data
  Button_part start (.out(start_out));
  Clock clk (.out(clk_out));
  Button_part Reset (.out(Reset_out));
  Button sync (.bt_in(data_av_out), .clk(clk_out), .reset(Reset_out), .bt_out(sync_bt_out));
  CORDIC cordic_1 (
    .data(data), .Adres(cordic_1_adres), .Anglestable(register_1_q), .start(start_out),
    .data_av(sync_bt_out), .clk(clk_out), .rst(Reset_out), .DONE(DONE), .sin(sin), .cos(cos),
    .state(next_state), .en(cordic_1_en));
  // Probe on sin
  // Probe on cos
  ROM #(.addrWidth(5), .dataWidth(32)) rom_1 (.addr(cordic_1_adres), .data(rom_1_data), .sel(cordic_1_en));
  Register #(.width(32)) register_1 (
    .D(rom_1_data), .en(cordic_1_en), .Q(register_1_q), .clk(clk_out), .clr(Reset_out));

  // Notes on the sheet:
  //   contents of rom_1 (hex, n*v repeats v):
  //   2d000000 1a90a731 e094740 7200112 3938aa6 1ca3794 e52a1a 7296d7 394ba5 1ca5d9 e52ed 72976 394bb
  //   1ca5d e52e 7297 394b 1ca5 e52 729 394 1ca e5 72 39 1c e 7 3 1
  //   Pedro Martins Basso
  //   Lucas Lauck
  //   Luis Felipe de Deus
endmodule

module DataPath (
  input  [7:0] data,
  input  in_2,
  input  in_3,
  input  [31:0] AngleTable_i,
  input  in_5,
  input  in_6,
  input  in_7,
  input  in_8,
  input  in_9,
  input  in_10,
  input  in_11,
  input  in_12,
  input  in_13,
  input  in_14,
  input  in_15,
  input  in_16,
  input  in_17,
  input  in_18,
  input  in_19,
  input  in_20,
  input  in_21,
  output [31:0] cos,
  output [31:0] sin,
  output if_else,
  output condicao,
  output [4:0] Adres
);

  wire and_1_out;
  wire [30:0] demultiplexer_2_out2;
  wire [31:0] adder_1_out, angle_q, bit_extender_1_out, demultiplexer_1_out0, demultiplexer_1_out1,
       demultiplexer_2_out0, demultiplexer_2_out1, demultiplexer_2_out3, demultiplexer_2_out4,
       demultiplexer_2_out5, demultiplexer_2_out6, it_q, multiplexer_1_out, multiplexer_2_out,
       multiplexer_3_out, multiplexer_4_out, multiplexer_5_out, multiplexer_6_out, not_1_out, not_2_out,
       not_3_out, not_4_out, shifter_1_out, shifter_2_out, sumAngle_q, X_NEW_q, x_q, Y_NEW_q, y_q;
  wire [31:5] i_q;

  Register #(.width(32)) X_NEW (.D(demultiplexer_2_out0), .en(in_5), .Q(X_NEW_q), .clk(in_2), .clr(in_3));
  Register #(.width(32)) Y_NEW (.D(demultiplexer_2_out1), .en(in_8), .Q(Y_NEW_q), .clk(in_2), .clr(in_3));
  Register #(.width(32)) sumAngle (.D(multiplexer_6_out), .en(in_9), .Q(sumAngle_q), .clk(in_2), .clr(in_3));
  Register #(.width(32)) it (.D(demultiplexer_1_out0), .en(in_14), .Q(it_q), .clk(in_2), .clr(in_3));
  assign bit_extender_1_out = {{24{1'b0}}, data};  // Bit_Extender bit_extender_1
  Multiplexer #(.width(32), .enable("false")) multiplexer_1 (
    .in0(X_NEW_q), .in1(32'h9b74ed), .out(multiplexer_1_out), .sel(in_13));
  Demultiplexer #(.width(32), .enable("false")) demultiplexer_1 (
    .out0(demultiplexer_1_out0), .out1(demultiplexer_1_out1), .in(bit_extender_1_out), .sel(in_18));
  Register #(.width(32)) x (.D(multiplexer_1_out), .en(in_6), .Q(x_q), .clk(in_2), .clr(in_3));
  Register #(.width(32)) y (.D(Y_NEW_q), .en(in_19), .Q(y_q), .clk(in_2), .clr(in_3));
  Register #(.width(32)) u_cos (.D(x_q), .en(in_20), .Q(cos), .clk(in_2), .clr(in_3));
  Register #(.width(32)) u_sin (.D(y_q), .en(in_21), .Q(sin), .clk(in_2), .clr(in_3));
  Register #(.width(32)) angle (.D(shifter_1_out), .en(in_18), .Q(angle_q), .clk(in_2), .clr(in_3));
  Shifter #(.width(32)) shifter_1 (.in(demultiplexer_1_out1), .\dist (5'b11000), .out(shifter_1_out));
  assign not_1_out = ~angle_q;  // NOT_Gate not_1, 32 bits wide
  Multiplexer #(.width(32), .enable("false")) multiplexer_2 (.in0(x_q), .in1(y_q), .out(multiplexer_2_out), .sel(in_5));
  assign not_2_out = ~AngleTable_i;  // NOT_Gate not_2, 32 bits wide
  assign not_3_out = ~{i_q, Adres};  // NOT_Gate not_3, 32 bits wide
  Multiplexer #(.select(2), .width(32), .enable("false")) multiplexer_3 (
    .in0(multiplexer_5_out), .in1(32'h1), .in2(sumAngle_q), .in3(it_q), .out(multiplexer_3_out),
    .sel({in_10, in_11}));
  and and_1 (and_1_out, 1'b1, in_12);
  Multiplexer #(.select(3), .width(32), .enable("false")) multiplexer_4 (
    .in0(x_q), .in1(y_q), .in2(not_1_out), .in3(AngleTable_i), .in4(not_2_out), .in5({i_q, Adres}),
    .in6(not_3_out), .out(multiplexer_4_out), .sel({in_15, in_16, in_17}));  // open: in7
  Register #(.width(32)) i (.D(demultiplexer_2_out5), .en(in_19), .Q({i_q, Adres}), .clk(in_2), .clr(in_3));
  assign not_4_out = ~shifter_2_out;  // NOT_Gate not_4, 32 bits wide
  Multiplexer #(.width(32), .enable("false")) multiplexer_5 (
    .in0(not_4_out), .in1(shifter_2_out), .out(multiplexer_5_out), .sel(in_7));
  Shifter #(.width(32), .shift("ar")) shifter_2 (.in(multiplexer_2_out), .\dist (Adres), .out(shifter_2_out));
  Demultiplexer #(.select(3), .width(32), .enable("false")) demultiplexer_2 (
    .out0(demultiplexer_2_out0), .out1(demultiplexer_2_out1), .out2({if_else, demultiplexer_2_out2}),
    .out3(demultiplexer_2_out3), .out4(demultiplexer_2_out4), .out5(demultiplexer_2_out5),
    .out6(demultiplexer_2_out6), .in(adder_1_out), .sel({in_15, in_16, in_17}));  // open: out7
  Adder #(.width(32)) adder_1 (
    .a(multiplexer_3_out), .b(multiplexer_4_out), .out(adder_1_out), .cin(and_1_out));  // open: cout
  Multiplexer #(.width(32), .enable("false")) multiplexer_6 (
    .in0(demultiplexer_2_out3), .in1(demultiplexer_2_out4), .out(multiplexer_6_out), .sel(in_12));
  nor nor_1 (condicao, demultiplexer_2_out6[31], demultiplexer_2_out6[30], demultiplexer_2_out6[29], demultiplexer_2_out6[28], demultiplexer_2_out6[27], demultiplexer_2_out6[26], demultiplexer_2_out6[25], demultiplexer_2_out6[24], demultiplexer_2_out6[23], demultiplexer_2_out6[22], demultiplexer_2_out6[21], demultiplexer_2_out6[20], demultiplexer_2_out6[19], demultiplexer_2_out6[18], demultiplexer_2_out6[17], demultiplexer_2_out6[16], demultiplexer_2_out6[15], demultiplexer_2_out6[14], demultiplexer_2_out6[13], demultiplexer_2_out6[12], demultiplexer_2_out6[11], demultiplexer_2_out6[10], demultiplexer_2_out6[9], demultiplexer_2_out6[8], demultiplexer_2_out6[7], demultiplexer_2_out6[6], demultiplexer_2_out6[5], demultiplexer_2_out6[4], demultiplexer_2_out6[3], demultiplexer_2_out6[2], demultiplexer_2_out6[1], demultiplexer_2_out6[0]);

  // Other names for the same wires on the sheet: angle_en = in_18; clk = in_2; cos_t = in_20; i_en = in_19;
  //   it_en = in_14; mux_sm1[1:0] = {in_10, in_11}; mux_sm2[2:0] = {in_15, in_16, in_17}; mux_x = in_13; rst = in_3;
  //   sin_t = in_21; sinal_desl = in_7; sub = in_12; sumAngle_en = in_9; x_en = in_6; x_new_en = in_5;
  //   y_new_en = in_8
endmodule

module ControlPath (
  input  start,
  input  data_av,
  input  condicao,
  input  if_else,
  input  in_5,
  input  in_6,
  output [3:0] out_7,
  output x_new__en,
  output x_en,
  output sinal_desl,
  output y_new_en,
  output sumAngle_en,
  output mux_sm1_1,
  output mux_sm1_0,
  output sub,
  output mux_x,
  output it_en,
  output mux_sm2_2,
  output mux_sm2_1,
  output mux_sm2_0,
  output angle_en,
  output i_en,
  output Done,
  output cos,
  output sin
);

  wire d_ff_1_q, d_ff_2_q, d_ff_3_q, d_ff_4_q;

  Nextstate nextstate_1 (
    .Q3(d_ff_1_q), .Q2(d_ff_2_q), .Q1(d_ff_3_q), .Q0(d_ff_4_q), .start(start), .data_av(data_av),
    .condicao(condicao), .if_else(if_else), .Q3p(out_7[3]), .Q2p(out_7[2]), .Q1p(out_7[1]), .Q0p(out_7[0]));
  D_Flip_Flop d_ff_1 (.clk(in_5), .D(out_7[3]), .Q(d_ff_1_q), .en(1'b1), .reset(in_6));  // open: Qn, preset
  D_Flip_Flop d_ff_2 (.clk(in_5), .D(out_7[2]), .Q(d_ff_2_q), .en(1'b1), .reset(in_6));  // open: Qn, preset
  D_Flip_Flop d_ff_3 (.clk(in_5), .D(out_7[1]), .Q(d_ff_3_q), .en(1'b1), .reset(in_6));  // open: Qn, preset
  D_Flip_Flop d_ff_4 (.clk(in_5), .D(out_7[0]), .Q(d_ff_4_q), .en(1'b1), .reset(in_6));  // open: Qn, preset
  Output output_1 (
    .Q3(d_ff_1_q), .Q2(d_ff_2_q), .Q1(d_ff_3_q), .Q0(d_ff_4_q), .x_new__en(x_new__en), .x_en(x_en),
    .sinal_desl(sinal_desl), .y_new_en(y_new_en), .sumAngle_en(sumAngle_en), .mux_sm1_1(mux_sm1_1),
    .mux_sm1_0(mux_sm1_0), .it_en(it_en), .mux_sm2_2(mux_sm2_2), .mux_sm2_1(mux_sm2_1),
    .mux_sm2_0(mux_sm2_0), .angle_en(angle_en), .i_en(i_en), .cos(cos), .sin(sin), .Done(Done), .sub(sub),
    .mux_x(mux_x));

  // Other names for the same wires on the sheet: clk = in_5; rst = in_6
endmodule

module CORDIC (
  input  data_av,
  input  start,
  input  rst,
  input  clk,
  input  [31:0] Anglestable,
  input  [7:0] data,
  output DONE,
  output en,
  output [31:0] sin,
  output [31:0] cos,
  output [3:0] state,
  output [4:0] Adres
);

  wire controlpath_1_angle_en, controlpath_1_cos, controlpath_1_i_en, controlpath_1_it_en,
       controlpath_1_mux_sm1_0, controlpath_1_mux_sm1_1, controlpath_1_mux_sm2_0, controlpath_1_mux_sm2_1,
       controlpath_1_mux_sm2_2, controlpath_1_mux_x, controlpath_1_sin, controlpath_1_sinal_desl,
       controlpath_1_sub, controlpath_1_sumangle_en, controlpath_1_x_en, controlpath_1_x_new__en,
       controlpath_1_y_new_en, datapath_1_condicao, datapath_1_if_else;

  ControlPath controlpath_1 (
    .start(start), .data_av(data_av), .condicao(datapath_1_condicao), .if_else(datapath_1_if_else),
    .in_5(clk), .in_6(rst), .out_7(state), .x_new__en(controlpath_1_x_new__en), .x_en(controlpath_1_x_en),
    .sinal_desl(controlpath_1_sinal_desl), .y_new_en(controlpath_1_y_new_en),
    .sumAngle_en(controlpath_1_sumangle_en), .mux_sm1_1(controlpath_1_mux_sm1_1),
    .mux_sm1_0(controlpath_1_mux_sm1_0), .sub(controlpath_1_sub), .mux_x(controlpath_1_mux_x),
    .it_en(controlpath_1_it_en), .mux_sm2_2(controlpath_1_mux_sm2_2), .mux_sm2_1(controlpath_1_mux_sm2_1),
    .mux_sm2_0(controlpath_1_mux_sm2_0), .angle_en(controlpath_1_angle_en), .i_en(controlpath_1_i_en),
    .Done(DONE), .cos(controlpath_1_cos), .sin(controlpath_1_sin));
  DataPath datapath_1 (
    .data(data), .if_else(datapath_1_if_else), .condicao(datapath_1_condicao), .Adres(Adres),
    .in_5(controlpath_1_x_new__en), .in_3(rst), .in_2(clk), .in_13(controlpath_1_mux_x),
    .in_6(controlpath_1_x_en), .in_7(controlpath_1_sinal_desl), .in_8(controlpath_1_y_new_en),
    .in_19(controlpath_1_i_en), .in_9(controlpath_1_sumangle_en), .in_14(controlpath_1_it_en),
    .in_18(controlpath_1_angle_en), .AngleTable_i(Anglestable), .in_10(controlpath_1_mux_sm1_1),
    .in_11(controlpath_1_mux_sm1_0), .in_15(controlpath_1_mux_sm2_2), .in_16(controlpath_1_mux_sm2_1),
    .in_17(controlpath_1_mux_sm2_0), .in_20(controlpath_1_cos), .cos(cos), .in_21(controlpath_1_sin),
    .in_12(controlpath_1_sub), .sin(sin));

  assign en = 1'b1;
endmodule

module Output (
  input  Q3,
  input  Q2,
  input  Q1,
  input  Q0,
  output x_new__en,
  output x_en,
  output sinal_desl,
  output y_new_en,
  output sumAngle_en,
  output mux_sm1_1,
  output mux_sm1_0,
  output sub,
  output mux_x,
  output it_en,
  output mux_sm2_2,
  output mux_sm2_1,
  output mux_sm2_0,
  output angle_en,
  output i_en,
  output Done,
  output cos,
  output sin
);

  Output1 output1_1 (
    .Q3(Q3), .x_new_en(x_new__en), .Q2(Q2), .x_en(x_en), .Q1(Q1), .Q0(Q0), .sinal_desl(sinal_desl),
    .y_new_en(y_new_en), .sumAngle_en(sumAngle_en), .mux_sm1_1(mux_sm1_1), .mux_sm1_0(mux_sm1_0), .sub(sub));
  Output2 output2_1 (
    .Q3(Q3), .Q2(Q2), .mux_x(mux_x), .Q1(Q1), .Q0(Q0), .it_en(it_en), .mux_sm2_2(mux_sm2_2),
    .mux_sm2_1(mux_sm2_1), .mux_sm2_0(mux_sm2_0), .angle_en(angle_en), .i_en(i_en), .Done(Done), .cos(cos),
    .sin(sin));
endmodule

module Output1 (
  input  Q3,
  input  Q2,
  input  Q1,
  input  Q0,
  output x_new_en,
  output x_en,
  output sinal_desl,
  output y_new_en,
  output sumAngle_en,
  output mux_sm1_1,
  output mux_sm1_0,
  output sub
);

  wire and_3_out, and_4_out, and_5_out, and_6_out, and_7_out, and_8_out, and_9_out, and_10_out, and_11_out,
       and_12_out, and_13_out, and_14_out, not_1_out, not_2_out, not_3_out, not_4_out, not_5_out, not_6_out,
       not_7_out, not_8_out, not_9_out, not_10_out, not_11_out, not_12_out, not_13_out, not_14_out,
       not_15_out, not_16_out, not_17_out, not_18_out, not_19_out, not_20_out, not_21_out;

  not not_1 (not_1_out, Q1);
  and and_1 (x_new_en, not_1_out, Q0);
  not not_2 (not_2_out, Q2);
  not not_3 (not_3_out, Q1);
  and and_2 (x_en, not_2_out, not_3_out, not_4_out);
  not not_4 (not_4_out, Q0);
  not not_5 (not_5_out, Q3);
  and and_3 (and_3_out, not_5_out, not_6_out);
  not not_6 (not_6_out, Q0);
  not not_7 (not_7_out, Q2);
  and and_4 (and_4_out, not_7_out, not_8_out);
  not not_8 (not_8_out, Q1);
  not not_9 (not_9_out, Q1);
  and and_5 (and_5_out, not_9_out, Q0);
  and and_6 (and_6_out, Q1, not_10_out);
  not not_10 (not_10_out, Q0);
  and and_7 (and_7_out, Q2, Q1, Q0);
  and and_8 (and_8_out, Q3, Q1, Q0);
  not not_11 (not_11_out, Q3);
  not not_12 (not_12_out, Q1);
  and and_9 (and_9_out, not_11_out, not_12_out, not_13_out);
  not not_13 (not_13_out, Q0);
  and and_10 (and_10_out, Q1, Q0);
  not not_14 (not_14_out, Q3);
  and and_11 (and_11_out, not_14_out, not_15_out);
  not not_15 (not_15_out, Q2);
  not not_16 (not_16_out, Q2);
  and and_12 (and_12_out, not_16_out, not_17_out, not_18_out);
  not not_17 (not_17_out, Q1);
  not not_18 (not_18_out, Q0);
  not not_19 (not_19_out, Q3);
  and and_13 (and_13_out, not_19_out, not_20_out);
  not not_20 (not_20_out, Q1);
  not not_21 (not_21_out, Q2);
  and and_14 (and_14_out, not_21_out, Q1);
  or or_1 (sinal_desl, and_3_out, and_4_out);
  or or_2 (y_new_en, and_5_out, and_6_out);
  or or_3 (sumAngle_en, and_7_out, and_8_out);
  or or_4 (mux_sm1_1, and_9_out, and_10_out);
  or or_5 (mux_sm1_0, and_11_out, and_12_out);
  or or_6 (sub, and_13_out, and_14_out);
endmodule

module Output2 (
  input  Q3,
  input  Q2,
  input  Q1,
  input  Q0,
  output mux_x,
  output it_en,
  output mux_sm2_2,
  output mux_sm2_1,
  output mux_sm2_0,
  output angle_en,
  output i_en,
  output Done,
  output cos,
  output sin
);

  wire and_1_out, and_2_out, and_3_out, and_5_out, and_6_out, and_7_out, and_8_out, and_9_out, and_10_out,
       not_1_out, not_2_out, not_3_out, not_4_out, not_5_out, not_6_out, not_7_out, not_8_out, not_9_out,
       not_10_out, not_11_out, not_12_out, not_13_out, not_14_out, not_15_out, not_16_out, not_17_out,
       not_18_out, not_19_out, not_20_out, not_21_out, not_22_out, not_23_out, not_24_out, not_25_out,
       not_26_out, not_27_out, not_28_out, not_29_out, not_30_out;

  not not_1 (not_1_out, Q3);
  and and_1 (and_1_out, not_1_out, not_2_out);
  not not_2 (not_2_out, Q2);
  not not_3 (not_3_out, Q3);
  not not_4 (not_4_out, Q1);
  and and_2 (and_2_out, not_3_out, not_4_out, Q0);
  not not_5 (not_5_out, Q2);
  and and_3 (and_3_out, not_5_out, Q1);
  not not_6 (not_6_out, Q3);
  and and_4 (it_en, not_6_out, not_7_out, not_8_out);
  not not_7 (not_7_out, Q2);
  not not_8 (not_8_out, Q0);
  not not_9 (not_9_out, Q2);
  not not_10 (not_10_out, Q1);
  and and_5 (and_5_out, not_9_out, not_10_out, not_11_out);
  not not_11 (not_11_out, Q0);
  not not_12 (not_12_out, Q2);
  and and_6 (and_6_out, not_12_out, Q1, Q0);
  not not_13 (not_13_out, Q3);
  not not_14 (not_14_out, Q1);
  and and_7 (and_7_out, not_13_out, not_14_out, not_15_out);
  not not_15 (not_15_out, Q0);
  not not_16 (not_16_out, Q3);
  and and_8 (and_8_out, not_16_out, Q1, Q0);
  not not_17 (not_17_out, Q2);
  and and_9 (and_9_out, not_17_out, not_18_out);
  not not_18 (not_18_out, Q0);
  and and_10 (and_10_out, Q2, Q1);
  not not_19 (not_19_out, Q3);
  not not_20 (not_20_out, Q2);
  not not_21 (not_21_out, Q1);
  not not_22 (not_22_out, Q2);
  not not_23 (not_23_out, Q1);
  not not_24 (not_24_out, Q0);
  not not_25 (not_25_out, Q1);
  not not_26 (not_26_out, Q0);
  not not_27 (not_27_out, Q1);
  not not_28 (not_28_out, Q0);
  not not_29 (not_29_out, Q1);
  not not_30 (not_30_out, Q0);
  or or_1 (mux_x, and_1_out, and_2_out, and_3_out);
  or or_2 (mux_sm2_2, and_5_out, and_6_out);
  or or_3 (mux_sm2_1, and_7_out, and_8_out);
  or or_4 (mux_sm2_0, and_9_out, and_10_out);
  and and_11 (angle_en, not_19_out, not_20_out, not_21_out, Q0);
  and and_12 (i_en, Q3, not_22_out, not_23_out, not_24_out);
  and and_13 (Done, Q3, not_25_out, not_26_out, Q2, Q3);
  and and_14 (cos, Q3, Q2, not_27_out, not_28_out);
  and and_15 (sin, Q3, Q2, not_29_out, not_30_out);
endmodule

module Nextstate (
  input  Q3,
  input  Q2,
  input  Q1,
  input  Q0,
  input  start,
  input  data_av,
  input  condicao,
  input  if_else,
  output Q3p,
  output Q2p,
  output Q1p,
  output Q0p
);

  wire and_1_out, and_2_out, and_3_out, and_4_out, and_5_out, and_6_out, and_7_out, and_8_out, and_9_out,
       and_10_out, and_11_out, and_12_out, and_13_out, and_14_out, and_15_out, and_16_out, and_17_out,
       and_18_out, and_19_out, and_20_out, and_21_out, not_1_out, not_2_out, not_3_out, not_4_out, not_5_out,
       not_6_out, not_7_out, not_8_out, not_9_out, not_10_out, not_11_out, not_12_out, not_13_out,
       not_14_out, not_15_out, not_16_out, not_17_out, not_18_out, not_19_out, not_20_out, not_21_out,
       not_22_out, not_23_out, not_24_out;

  not not_1 (not_1_out, Q1);
  not not_2 (not_2_out, Q0);
  not not_3 (not_3_out, if_else);
  not not_4 (not_4_out, Q3);
  not not_5 (not_5_out, Q2);
  not not_6 (not_6_out, Q1);
  not not_7 (not_7_out, Q1);
  not not_8 (not_8_out, Q0);
  not not_9 (not_9_out, Q2);
  not not_10 (not_10_out, Q1);
  not not_11 (not_11_out, Q0);
  not not_12 (not_12_out, Q3);
  not not_13 (not_13_out, Q1);
  not not_14 (not_14_out, Q2);
  not not_15 (not_15_out, Q1);
  not not_16 (not_16_out, Q1);
  not not_17 (not_17_out, Q0);
  not not_18 (not_18_out, Q3);
  not not_19 (not_19_out, Q2);
  not not_20 (not_20_out, Q1);
  not not_21 (not_21_out, data_av);
  not not_22 (not_22_out, Q0);
  not not_23 (not_23_out, Q0);
  not not_24 (not_24_out, Q0);
  and and_1 (and_1_out, Q1, Q0, condicao);
  and and_2 (and_2_out, Q2, not_1_out, not_2_out, not_3_out);
  and and_3 (and_3_out, Q2, Q1, Q0);
  and and_4 (and_4_out, Q3, Q0);
  and and_5 (and_5_out, Q3, Q1);
  and and_6 (and_6_out, Q3, Q2);
  and and_7 (and_7_out, not_4_out, not_5_out, Q1, Q0);
  and and_8 (and_8_out, Q2, not_6_out, if_else);
  and and_9 (and_9_out, Q2, not_7_out, Q0);
  and and_10 (and_10_out, Q2, Q1, not_8_out);
  and and_11 (and_11_out, Q3, Q2);
  and and_12 (and_12_out, not_9_out, not_10_out, Q0, data_av);
  and and_13 (and_13_out, Q1, not_11_out);
  and and_14 (and_14_out, not_12_out, Q2, not_13_out, Q0);
  and and_15 (and_15_out, Q3, not_14_out, not_15_out);
  and and_16 (and_16_out, not_16_out, not_17_out, data_av);
  and and_17 (and_17_out, not_18_out, not_19_out, not_20_out, Q0, not_21_out);
  and and_18 (and_18_out, Q1, not_22_out, start);
  and and_19 (and_19_out, Q2, not_23_out);
  and and_20 (and_20_out, Q3, not_24_out);
  and and_21 (and_21_out, Q3, Q2);
  or or_1 (Q3p, and_1_out, and_2_out, and_3_out, and_4_out, and_5_out, and_6_out);
  or or_2 (Q2p, and_7_out, and_8_out, and_9_out, and_10_out, and_11_out);
  or or_3 (Q1p, and_12_out, and_13_out, and_14_out, and_15_out);
  or or_4 (Q0p, and_16_out, and_17_out, and_18_out, and_19_out, and_20_out, and_21_out);
endmodule

module Button (
  input  bt_in,
  input  clk,
  input  reset,
  output bt_out
);

  wire and_1_out, and_2_out, FF0_q, FF1_q, not_1_out, not_2_out, not_3_out, or_1_out;

  or or_1 (or_1_out, FF1_q, FF0_q);
  not not_1 (not_1_out, FF1_q);
  not not_2 (not_2_out, FF0_q);
  and and_1 (and_1_out, or_1_out, bt_in);
  and and_2 (and_2_out, not_1_out, not_2_out, bt_in);
  D_Flip_Flop FF1 (.clk(clk), .D(and_1_out), .Q(FF1_q), .reset(reset));  // open: Qn, preset, en
  D_Flip_Flop FF0 (.clk(clk), .D(and_2_out), .Q(FF0_q), .reset(reset));  // open: Qn, preset, en
  not not_3 (not_3_out, FF1_q);
  and and_3 (bt_out, not_3_out, FF0_q);
endmodule
