// Logisim project T1_Projetos_V1.circ as structural Verilog: 2 circuits, main circuit main
module main (
  input  [7:0] Data,
  input  [2:0] in_2,
  input  in_3,
  input  [3:0] in_4,
  input  Rd_ROM,
  input  Sel_i,
  input  in_7,
  input  in_8,
  input  in_9,
  input  in_10,
  input  in_11,
  input  in_12,
  input  in_13,
  input  in_14,
  input  in_15,
  input  in_16,
  input  in_17,
  input  in_18,
  input  in_19,
  input  in_20
);

  wire CLK, Flag_N, Zero;
  wire [30:0] Out_Soma;
  wire [31:0] bit_extender_1_out, i, multiplexer_1_out, multiplexer_2_out, multiplexer_3_out,
       multiplexer_4_out, multiplexer_5_out, multiplexer_6_out, not_1_out, not_2_out, not_3_out, not_4_out,
       not_5_out, Reg_Angle_q, Reg_Int_q, Reg_Sinc_q, Reg_SumAngle_q, rom_1_data, shifter_1_out,
       shifter_2_out, X, x_New_q, Y, y__i, y_New_q;

  assign bit_extender_1_out = {{24{1'b0}}, Data};  // Bit_Extender bit_extender_1
  Shifter #(.width(32)) shifter_1 (.in(bit_extender_1_out), .\dist (5'b11000), .out(shifter_1_out));
  Multiplexer #(.width(32), .enable("false")) multiplexer_1 (
    .in0({32{1'b0}}), .in1({Flag_N, Out_Soma}), .out(multiplexer_1_out), .sel(in_8));
  Multiplexer #(.width(32), .enable("false")) multiplexer_2 (
    .in0(32'h9b74ed), .in1(x_New_q), .out(multiplexer_2_out), .sel(in_10));
  Multiplexer #(.width(32), .enable("false")) multiplexer_3 (
    .in0({32{1'b0}}), .in1(y_New_q), .out(multiplexer_3_out), .sel(in_12));
  Multiplexer #(.width(32), .enable("false")) multiplexer_4 (
    .in0({32{1'b0}}), .in1({Flag_N, Out_Soma}), .out(multiplexer_4_out), .sel(Sel_i));
  Register #(.width(32)) Reg_Angle (.D(shifter_1_out), .en(in_7), .Q(Reg_Angle_q), .clk(CLK), .clr(in_20));
  Register #(.width(32)) Reg_Int (.D(bit_extender_1_out), .en(in_9), .Q(Reg_Int_q), .clk(CLK), .clr(in_20));
  Register #(.width(32)) Reg_SumAngle (.D(multiplexer_1_out), .en(in_11), .Q(Reg_SumAngle_q), .clk(CLK), .clr(in_20));
  Register #(.width(32)) u_X (.D(multiplexer_2_out), .en(in_13), .Q(X), .clk(CLK), .clr(in_20));
  Register #(.width(32)) u_Y (.D(multiplexer_3_out), .en(in_15), .Q(Y), .clk(CLK), .clr(in_20));
  Register #(.width(32)) u_i (.D(multiplexer_4_out), .en(in_16), .Q(i), .clk(CLK), .clr(in_20));
  Register #(.width(32)) x_New (.D({Flag_N, Out_Soma}), .en(in_17), .Q(x_New_q), .clk(CLK), .clr(in_20));
  Register #(.width(32)) y_New (.D({Flag_N, Out_Soma}), .en(in_18), .Q(y_New_q), .clk(CLK), .clr(in_20));
  // Probe on Reg_Angle_q
  Shifter #(.width(32), .shift("ar")) shifter_2 (.in(X), .\dist (i[4:0]), .out(shifter_2_out));
  Clock clock_1 (.out(CLK));
  Shifter #(.width(32), .shift("ar")) shifter_3 (.in(Y), .\dist (i[4:0]), .out(y__i));
  assign not_1_out = ~y__i;  // NOT_Gate not_1, 32 bits wide
  assign not_2_out = ~shifter_2_out;  // NOT_Gate not_2, 32 bits wide
  assign not_3_out = ~i;  // NOT_Gate not_3, 32 bits wide
  assign not_4_out = ~Reg_Angle_q;  // NOT_Gate not_4, 32 bits wide
  assign not_5_out = ~Reg_Sinc_q;  // NOT_Gate not_5, 32 bits wide
  Multiplexer #(.select(3), .width(32), .enable("false")) multiplexer_5 (
    .in0(32'h1), .in1(Reg_Int_q), .in2(Reg_SumAngle_q), .in3(X), .in4(Y), .out(multiplexer_5_out), .sel(in_2));  // open: in5, in6, in7
  Multiplexer #(.select(4), .width(32), .enable("false")) multiplexer_6 (
    .in0(not_1_out), .in1(not_2_out), .in2(not_3_out), .in3(not_4_out), .in4(not_5_out), .in5(shifter_2_out),
    .in6(y__i), .in7(i), .in8(Reg_Angle_q), .in9(Reg_Sinc_q), .out(multiplexer_6_out), .sel(in_4));  // open: in10, in11, in12, in13, in14, in15
  Adder #(.width(32)) adder_1 (
    .a(multiplexer_5_out), .b(multiplexer_6_out), .out({Flag_N, Out_Soma}), .cin(in_3));  // open: cout
  // Probe on {Flag_N, Out_Soma}
  ROM #(.addrWidth(5), .dataWidth(32)) rom_1 (.addr(i[4:0]), .data(rom_1_data), .sel(Rd_ROM));
  Register #(.width(32)) Reg_Sinc (.D(rom_1_data), .en(in_19), .Q(Reg_Sinc_q), .clk(CLK), .clr(in_20));
  // Probe on Flag_N
  nor nor_1 (Zero, Out_Soma[0], Out_Soma[1], Out_Soma[2], Out_Soma[3], Out_Soma[4], Out_Soma[5], Out_Soma[6], Out_Soma[7], Out_Soma[8], Out_Soma[9], Out_Soma[10], Out_Soma[11], Out_Soma[12], Out_Soma[13], Out_Soma[14], Out_Soma[15], Out_Soma[16], Out_Soma[17], Out_Soma[18], Out_Soma[19], Out_Soma[20], Out_Soma[21], Out_Soma[22], Out_Soma[23], Out_Soma[24], Out_Soma[25], Out_Soma[26], Out_Soma[27], Out_Soma[28], Out_Soma[29], Out_Soma[30], Flag_N);
  // Probe on Zero

  // Other names for the same wires on the sheet: GND_i = in_14; GND_Sum = in_8; Out_Soma[31] = Flag_N; RST = in_20;
  //   Sel_x = in_10; Sel_y = in_12; Wr_Angle = in_7; Wr_i = in_16; Wr_Int = in_9; Wr_Sinc = in_19; Wr_Sum = in_11;
  //   Wr_x = in_13; Wr_xnew = in_17; Wr_y = in_15; Wr_ynew = in_18

  // Notes on the sheet:
  //   Escrita nos Registradores
  //   Sinal de controle do Mux
  //   contents of rom_1 (hex, n*v repeats v):
  //   2d000000 1a90a731 e094740 7200112 3938aa6 1ca3794 e52a1a 7296d7 394ba5 1ca5d9 e52ed 72976 394bb
  //   1ca5d e52e 7297 394b 1ca5 e52 729 394 1ca e5 72 39 1c e 7 3 1
endmodule

module controlPath (
  input  Q3,
  input  Q2,
  input  Q1,
  input  Q0,
  input  Data_AV,
  input  Start,
  input  Zero,
  input  N,
  output q3_2,
  output q2_2,
  output q1_2,
  output q0_2,
  output done
);

  wire and_1_out, and_2_out, and_3_out, and_4_out, and_5_out, and_6_out, and_7_out, and_8_out, and_9_out,
       and_10_out, and_11_out, and_12_out, and_13_out, and_14_out, and_15_out, and_16_out, and_17_out,
       and_18_out, and_19_out, and_20_out, and_21_out, and_22_out, and_23_out, and_24_out, and_25_out,
       and_26_out, not_1_out, not_2_out, not_3_out, not_4_out, not_5_out, not_6_out, not_7_out, not_8_out,
       not_9_out, not_10_out, not_11_out, not_12_out, not_13_out, not_14_out, not_15_out, not_16_out,
       not_17_out, not_18_out, not_19_out, not_20_out, not_21_out, not_22_out, not_23_out, not_24_out,
       not_25_out, not_26_out, not_27_out, not_28_out, not_29_out, not_30_out, not_31_out, not_32_out,
       not_33_out, not_34_out, not_35_out, not_36_out, not_37_out, not_38_out, not_39_out, not_40_out,
       not_41_out, not_42_out, not_43_out, not_44_out, not_45_out, not_46_out, not_47_out, not_48_out,
       not_49_out, not_50_out, not_51_out, not_52_out;

  not not_1 (not_1_out, Q3);
  and and_1 (and_1_out, not_1_out, Q2, Q0);
  and and_2 (and_2_out, Q2, Q1);
  and and_3 (and_3_out, Q3, not_2_out);
  not not_2 (not_2_out, Q2);
  and and_4 (and_4_out, Q3, Q0, not_3_out);
  not not_3 (not_3_out, Start);
  not not_4 (not_4_out, Q2);
  not not_5 (not_5_out, Q2);
  not not_6 (not_6_out, Q3);
  not not_7 (not_7_out, Q1);
  not not_8 (not_8_out, Q1);
  not not_9 (not_9_out, Start);
  not not_10 (not_10_out, Q0);
  not not_11 (not_11_out, Data_AV);
  not not_12 (not_12_out, Start);
  not not_13 (not_13_out, Q2);
  not not_14 (not_14_out, Q1);
  not not_15 (not_15_out, Q3);
  not not_16 (not_16_out, Q2);
  not not_17 (not_17_out, Q0);
  not not_18 (not_18_out, Q3);
  not not_19 (not_19_out, Q2);
  not not_20 (not_20_out, Zero);
  not not_21 (not_21_out, N);
  not not_22 (not_22_out, Q1);
  not not_23 (not_23_out, Q0);
  not not_24 (not_24_out, Q2);
  not not_25 (not_25_out, Q1);
  not not_26 (not_26_out, Q2);
  not not_27 (not_27_out, Q1);
  not not_28 (not_28_out, Q0);
  not not_29 (not_29_out, Q3);
  not not_30 (not_30_out, Q1);
  not not_31 (not_31_out, Data_AV);
  not not_32 (not_32_out, Q3);
  not not_33 (not_33_out, Q0);
  not not_34 (not_34_out, Q3);
  not not_35 (not_35_out, Q2);
  not not_36 (not_36_out, N);
  not not_37 (not_37_out, Q3);
  not not_38 (not_38_out, Q1);
  not not_39 (not_39_out, N);
  not not_40 (not_40_out, Q3);
  not not_41 (not_41_out, Q1);
  not not_42 (not_42_out, Q1);
  not not_43 (not_43_out, Start);
  not not_44 (not_44_out, Q0);
  not not_45 (not_45_out, Q1);
  not not_46 (not_46_out, Q0);
  not not_47 (not_47_out, Q2);
  not not_48 (not_48_out, Q1);
  not not_49 (not_49_out, Zero);
  not not_50 (not_50_out, N);
  not not_51 (not_51_out, Q3);
  not not_52 (not_52_out, Q1);
  or or_1 (q3_2, and_1_out, and_2_out, and_3_out, and_4_out);
  and and_5 (and_5_out, not_4_out, Q1, Q0, N);
  and and_6 (and_6_out, not_5_out, Q1, Q0, Zero);
  and and_7 (and_7_out, not_6_out, Q2, not_7_out);
  and and_8 (and_8_out, Q2, not_8_out, Q0, not_9_out);
  and and_9 (and_9_out, Q3, Q1, not_10_out);
  and and_10 (and_10_out, Q3, Q1, not_11_out);
  and and_11 (and_11_out, Q3, Q1, not_12_out);
  and and_12 (and_12_out, not_13_out, not_14_out, Q0, Data_AV);
  and and_13 (and_13_out, not_15_out, not_16_out, Q1, not_17_out);
  and and_14 (and_14_out, not_18_out, not_19_out, Q1, not_20_out, not_21_out);
  and and_15 (and_15_out, Q2, not_22_out, not_23_out);
  and and_16 (and_16_out, Q3, not_24_out, not_25_out);
  and and_17 (and_17_out, not_26_out, not_27_out, not_28_out, Data_AV);
  and and_18 (and_18_out, not_29_out, not_30_out, Q0, not_31_out);
  and and_19 (and_19_out, not_32_out, Q1, not_33_out, Start);
  and and_20 (and_20_out, not_34_out, not_35_out, Q1, Q0, not_36_out);
  and and_21 (and_21_out, not_37_out, Q2, not_38_out, not_39_out);
  and and_22 (and_22_out, not_40_out, Q2, not_41_out, Q0);
  and and_23 (and_23_out, Q2, not_42_out, Q0, not_43_out);
  and and_24 (and_24_out, Q2, Q1, not_44_out);
  and and_25 (and_25_out, Q3, not_45_out, not_46_out);
  and and_26 (and_26_out, Q3, not_47_out, not_48_out, Data_AV, Start, not_49_out, not_50_out);
  and and_27 (done, not_51_out, Q2, not_52_out, Q0);
  or or_2 (q2_2, and_5_out, and_6_out, and_7_out, and_8_out, and_9_out, and_10_out, and_11_out);
  or or_3 (q1_2, and_12_out, and_13_out, and_14_out, and_15_out, and_16_out);
  or or_4 (q0_2, and_17_out, and_18_out, and_19_out, and_20_out, and_21_out, and_22_out, and_23_out, and_24_out, and_25_out, and_26_out);
endmodule
