// Logisim project Sorted_with_DEBUG.circ as structural Verilog: 8 circuits, main circuit Debug
module Data_Path (
  input  en_0,
  input  sel_0,
  input  clk,
  input  [15:0] v_0,
  input  [15:0] v_5,
  input  en_1,
  input  sel1_1,
  input  rst,
  input  [15:0] v_1,
  input  [15:0] v_6,
  input  en_2,
  input  sel0_1,
  input  even,
  input  sel1_2,
  input  en_3,
  input  [15:0] v_2,
  input  [15:0] v_7,
  input  sel0_2,
  input  en_4,
  input  sel1_3,
  input  [15:0] v_3,
  input  [15:0] v_8,
  input  en_5,
  input  sel0_3,
  input  sel1_4,
  input  en_6,
  input  [15:0] v_4,
  input  [15:0] v_9,
  input  sel0_4,
  input  en_7,
  input  sel1_5,
  input  en_8,
  input  sel0_5,
  input  en_9,
  input  sel1_6,
  input  sel0_6,
  input  sel1_7,
  input  sel0_7,
  input  sel1_8,
  input  sel0_8,
  input  sel_9,
  output lt_A,
  output BltA_A,
  output lt_B,
  output BltA_B,
  output lt_C,
  output BltA_C,
  output lt_D,
  output BltA_D,
  output lt_E,
  output BltA_E,
  output [15:0] reg_0,
  output [15:0] reg_5,
  output [15:0] reg_1,
  output [15:0] reg_6,
  output [15:0] reg_2,
  output [15:0] reg_7,
  output [15:0] reg3,
  output [15:0] reg_8,
  output [15:0] reg_4,
  output [15:0] reg_9
);

  wire equal_A, equal_B, equal_C, equal_D, equal_E;
  wire [15:0] multiplexer_1_out, multiplexer_2_out, multiplexer_3_out, multiplexer_4_out, multiplexer_5_out,
       multiplexer_6_out, multiplexer_7_out, multiplexer_8_out, multiplexer_9_out, multiplexer_10_out,
       multiplexer_11_out, multiplexer_12_out, multiplexer_13_out, multiplexer_14_out;

  Multiplexer #(.width(16), .enable("false")) multiplexer_1 (
    .in0(v_0), .in1(reg_1), .out(multiplexer_1_out), .sel(sel_0));
  Multiplexer #(.select(2), .width(16), .enable("false")) multiplexer_2 (
    .in0(v_1), .in1(reg_0), .in2(reg_2), .out(multiplexer_2_out), .sel({sel0_1, sel1_1}));  // open: in3
  Multiplexer #(.select(2), .width(16), .enable("false")) multiplexer_3 (
    .in0(v_2), .in1(reg_1), .in2(reg3), .out(multiplexer_3_out), .sel({sel0_2, sel1_2}));  // open: in3
  Multiplexer #(.select(2), .width(16), .enable("false")) multiplexer_4 (
    .in0(v_3), .in1(reg_2), .in2(reg_4), .out(multiplexer_4_out), .sel({sel0_3, sel1_3}));  // open: in3
  Multiplexer #(.select(2), .width(16), .enable("false")) multiplexer_5 (
    .in0(v_4), .in1(reg3), .in2(reg_5), .out(multiplexer_5_out), .sel({sel0_4, sel1_4}));  // open: in3
  Multiplexer #(.select(2), .width(16), .enable("false")) multiplexer_6 (
    .in0(v_5), .in1(reg_4), .in2(reg_6), .out(multiplexer_6_out), .sel({sel0_5, sel1_5}));  // open: in3
  Multiplexer #(.select(2), .width(16), .enable("false")) multiplexer_7 (
    .in0(v_6), .in1(reg_5), .in2(reg_7), .out(multiplexer_7_out), .sel({sel0_6, sel1_6}));  // open: in3
  Multiplexer #(.select(2), .width(16), .enable("false")) multiplexer_8 (
    .in0(v_7), .in1(reg_6), .in2(reg_8), .out(multiplexer_8_out), .sel({sel0_7, sel1_7}));  // open: in3
  Multiplexer #(.select(2), .width(16), .enable("false")) multiplexer_9 (
    .in0(v_8), .in1(reg_7), .in2(reg_9), .out(multiplexer_9_out), .sel({sel0_8, sel1_8}));  // open: in3
  Multiplexer #(.width(16), .enable("false")) multiplexer_10 (
    .in0(v_9), .in1(reg_8), .out(multiplexer_10_out), .sel(sel_9));
  Register #(.width(16)) register_1 (.D(multiplexer_1_out), .en(en_0), .Q(reg_0), .clk(clk), .clr(rst));
  Register #(.width(16)) register_2 (.D(multiplexer_2_out), .en(en_1), .Q(reg_1), .clk(clk), .clr(rst));
  Register #(.width(16)) register_3 (.D(multiplexer_3_out), .en(en_2), .Q(reg_2), .clk(clk), .clr(rst));
  Register #(.width(16)) register_4 (.D(multiplexer_4_out), .en(en_3), .Q(reg3), .clk(clk), .clr(rst));
  Register #(.width(16)) register_5 (.D(multiplexer_5_out), .en(en_4), .Q(reg_4), .clk(clk), .clr(rst));
  Register #(.width(16)) register_6 (.D(multiplexer_6_out), .en(en_5), .Q(reg_5), .clk(clk), .clr(rst));
  Register #(.width(16)) register_7 (.D(multiplexer_7_out), .en(en_6), .Q(reg_6), .clk(clk), .clr(rst));
  Register #(.width(16)) register_8 (.D(multiplexer_8_out), .en(en_7), .Q(reg_7), .clk(clk), .clr(rst));
  Register #(.width(16)) register_9 (.D(multiplexer_9_out), .en(en_8), .Q(reg_8), .clk(clk), .clr(rst));
  Register #(.width(16)) register_10 (.D(multiplexer_10_out), .en(en_9), .Q(reg_9), .clk(clk), .clr(rst));
  Multiplexer #(.width(16), .enable("false")) multiplexer_11 (
    .in0(reg_0), .in1(reg_2), .out(multiplexer_11_out), .sel(even));
  Multiplexer #(.width(16), .enable("false")) multiplexer_12 (
    .in0(reg_2), .in1(reg_4), .out(multiplexer_12_out), .sel(even));
  Multiplexer #(.width(16), .enable("false")) multiplexer_13 (
    .in0(reg_4), .in1(reg_6), .out(multiplexer_13_out), .sel(even));
  Multiplexer #(.width(16), .enable("false")) multiplexer_14 (
    .in0(reg_6), .in1(reg_8), .out(multiplexer_14_out), .sel(even));
  Comparator #(.width(16), .mode("unsigned")) comparator_1 (
    .a(reg_1), .b(multiplexer_11_out), .eq(equal_A), .lt(lt_A));  // open: gt
  Comparator #(.width(16), .mode("unsigned")) comparator_2 (
    .a(reg3), .b(multiplexer_12_out), .eq(equal_B), .lt(lt_B));  // open: gt
  Comparator #(.width(16), .mode("unsigned")) comparator_3 (
    .a(reg_5), .b(multiplexer_13_out), .eq(equal_C), .lt(lt_C));  // open: gt
  Comparator #(.width(16), .mode("unsigned")) comparator_4 (
    .a(reg_7), .b(multiplexer_14_out), .eq(equal_D), .lt(lt_D));  // open: gt
  Comparator #(.width(16), .mode("unsigned")) comparator_5 (.a(reg_8), .b(reg_9), .eq(equal_E), .lt(lt_E));  // open: gt
  nor nor_1 (BltA_A, equal_A, lt_A);
  nor nor_2 (BltA_B, equal_B, lt_B);
  nor nor_3 (BltA_C, equal_C, lt_C);
  nor nor_4 (BltA_D, equal_D, lt_D);
  nor nor_5 (BltA_E, equal_E, lt_E);

  // Other names for the same wires on the sheet: less_than_A = lt_A; less_than_B = lt_B; less_than_C = lt_C;
  //   less_than_D = lt_D; less_than_E = lt_E; R_0[15:0] = reg_0; R_1[15:0] = reg_1; R_2[15:0] = reg_2;
  //   R_3[15:0] = reg3; R_4[15:0] = reg_4; R_5[15:0] = reg_5; R_6[15:0] = reg_6; R_7[15:0] = reg_7; R_8[15:0] = reg_8;
  //   R_9[15:0] = reg_9; sel_1[1:0] = {sel0_1, sel1_1}; sel_2[1:0] = {sel0_2, sel1_2}; sel_3[1:0] = {sel0_3, sel1_3};
  //   sel_4[1:0] = {sel0_4, sel1_4}; sel_5[1:0] = {sel0_5, sel1_5}; sel_6[1:0] = {sel0_6, sel1_6};
  //   sel_7[1:0] = {sel0_7, sel1_7}; sel_8[1:0] = {sel0_8, sel1_8}
endmodule

module Control_Path (
  input  ltA,
  input  Blt_A,
  input  ltB,
  input  Blt_B,
  input  ltC,
  input  Blt_C,
  input  clk,
  input  ltD,
  input  Blt_D,
  input  ltE,
  input  Blt_E,
  input  rst,
  output en_0,
  output en_1,
  output en_2,
  output en_3,
  output en_4,
  output en_5,
  output en_6,
  output en_7,
  output en_8,
  output sorted,
  output en_9,
  output sel_0,
  output sel0_1,
  output sel1_1,
  output sel0_2,
  output sel1_2,
  output sel0_3,
  output sel1_3,
  output sel0_4,
  output sel1_4,
  output sel0_5,
  output sel1_5,
  output sel0_6,
  output sel1_6,
  output sel0_7,
  output sel1_7,
  output sel0_8,
  output sel1_8,
  output sel_9,
  output even
);

  wire finish_sorted, next_state_1_q0p, next_state_1_q1p, Q0p, Q1p;

  Next_State next_state_1 (
    .Q0(Q0p), .Q0p(next_state_1_q0p), .Q1(Q1p), .Q1p(next_state_1_q1p), .finish_sorted(finish_sorted),
    .sorted(sorted));
  D_Flip_Flop #(.Pre_Clr_Positions("LEGACY"), .enable("true"), .NewFFLayout("false")) u_Q0p (
    .clk(clk), .D(next_state_1_q0p), .Q(Q0p), .en(1'b1), .reset(rst));  // open: Qn, preset
  D_Flip_Flop #(.Pre_Clr_Positions("LEGACY"), .enable("true"), .NewFFLayout("false")) u_Q1p (
    .clk(clk), .D(next_state_1_q1p), .Q(Q1p), .en(1'b1), .reset(rst));  // open: Qn, preset
  Output output_1 (
    .en_0(en_0), .en_1(en_1), .en_2(en_2), .en_3(en_3), .en_4(en_4), .en_5(en_5), .en_6(en_6), .en_7(en_7),
    .en_8(en_8), .en_9(en_9), .sel_0(sel_0), .sel0_1(sel0_1), .sel1_1(sel1_1), .sel0_2(sel0_2),
    .sel1_2(sel1_2), .sel0_3(sel0_3), .sel1_3(sel1_3), .sel0_4(sel0_4), .sel1_4(sel1_4), .sel0_5(sel0_5),
    .sel1_5(sel1_5), .sel0_6(sel0_6), .sel1_6(sel1_6), .sel0_7(sel0_7), .sel1_7(sel1_7), .sel0_8(sel0_8),
    .sel1_8(sel1_8), .sel_9(sel_9), .Q0(Q0p), .Q1(Q1p), .clk(clk), .rst(rst), .ltA(ltA), .ltB(ltB),
    .ltC(ltC), .ltD(ltD), .Blt_A(Blt_A), .Blt_B(Blt_B), .Blt_C(Blt_C), .Blt_D(Blt_D), .Blt_E(Blt_E),
    .finish_sorted(finish_sorted), .even(even));
endmodule

// NextState
module Next_State (
  input  Q0,
  input  Q1,
  input  finish_sorted,
  output Q0p,
  output Q1p,
  output sorted
);

  wire and_1_out, not_1_out;

  or or_1 (Q0p, finish_sorted, Q1);
  not not_1 (not_1_out, Q1);
  and and_1 (and_1_out, Q0, Q1);
  or or_2 (Q1p, not_1_out, finish_sorted, Q0);
  or or_3 (sorted, finish_sorted, and_1_out);
endmodule

module Output (
  input  Q0,
  input  ltA,
  input  Blt_A,
  input  Q1,
  input  ltB,
  input  Blt_B,
  input  ltC,
  input  Blt_C,
  input  clk,
  input  ltD,
  input  Blt_D,
  input  rst,
  input  Blt_E,
  output en_0,
  output sel_0,
  output en_1,
  output sel0_1,
  output en_2,
  output sel1_1,
  output en_3,
  output sel0_2,
  output en_4,
  output sel1_2,
  output en_5,
  output sel0_3,
  output en_6,
  output sel1_3,
  output finish_sorted,
  output en_7,
  output sel0_4,
  output en_8,
  output sel1_4,
  output even,
  output en_9,
  output sel0_5,
  output sel1_5,
  output sel0_6,
  output sel1_6,
  output sel0_7,
  output sel1_7,
  output sel0_8,
  output sel1_8,
  output sel_9
);

  wire and_1_out, and_2_out, and_3_out, and_4_out, and_5_out, and_6_out, and_7_out, and_8_out, and_9_out,
       and_10_out, and_11_out, and_12_out, and_13_out, and_14_out, and_15_out, and_16_out, and_17_out,
       and_18_out, and_19_out, and_20_out, and_21_out, and_22_out, and_23_out, and_24_out, and_25_out,
       and_26_out, and_27_out, and_28_out, finish_odd, in_even, not_1_out, not_2_out, not_3_out, not_4_out,
       not_5_out, not_6_out, not_7_out, not_8_out, not_9_out, not_10_out, not_11_out, not_12_out, not_13_out,
       not_14_out, not_15_out, not_16_out, not_17_out, not_18_out, not_19_out, not_20_out, not_21_out,
       not_22_out, not_23_out, not_24_out, not_25_out, not_26_out, not_27_out, not_28_out, not_29_out,
       not_30_out, not_31_out, not_32_out, not_33_out, not_34_out, not_35_out, not_36_out, not_37_out,
       not_38_out, not_39_out, not_40_out, not_41_out, not_42_out, not_43_out, not_44_out, not_45_out,
       not_46_out, not_47_out, not_48_out, not_49_out, not_50_out, q_even;

  not not_1 (not_1_out, Q0);
  not not_2 (not_2_out, Q1);
  not not_3 (not_3_out, Q0);
  not not_4 (not_4_out, Q1);
  not not_5 (not_5_out, Q0);
  not not_6 (not_6_out, Q1);
  not not_7 (not_7_out, Q0);
  not not_8 (not_8_out, Q1);
  not not_9 (not_9_out, Q0);
  not not_10 (not_10_out, Q1);
  not not_11 (not_11_out, Q0);
  not not_12 (not_12_out, Q1);
  not not_13 (not_13_out, Q0);
  not not_14 (not_14_out, Q1);
  not not_15 (not_15_out, Q0);
  not not_16 (not_16_out, Q1);
  not not_17 (not_17_out, Q0);
  not not_18 (not_18_out, Q1);
  not not_19 (not_19_out, Q0);
  not not_20 (not_20_out, Q1);
  and and_1 (and_1_out, not_1_out, not_2_out);
  not not_21 (not_21_out, Q0);
  and and_2 (and_2_out, not_21_out, Q1, ltA);
  and and_3 (and_3_out, not_3_out, not_4_out);
  not not_22 (not_22_out, Q0);
  and and_4 (and_4_out, not_22_out, Q1, ltA);
  and and_5 (and_5_out, Q0, not_23_out, Blt_A);
  not not_23 (not_23_out, Q1);
  and and_6 (and_6_out, not_5_out, not_6_out);
  not not_24 (not_24_out, Q0);
  and and_7 (and_7_out, not_24_out, Q1, ltB);
  not not_25 (not_25_out, Q1);
  and and_8 (and_8_out, Q0, not_25_out, Blt_A);
  and and_9 (and_9_out, not_7_out, not_8_out);
  not not_26 (not_26_out, Q0);
  and and_10 (and_10_out, not_26_out, Q1, ltB);
  not not_27 (not_27_out, Q1);
  and and_11 (and_11_out, Q0, not_27_out, Blt_B);
  and and_12 (and_12_out, not_9_out, not_10_out);
  not not_28 (not_28_out, Q0);
  and and_13 (and_13_out, not_28_out, Q1, ltC);
  not not_29 (not_29_out, Q1);
  and and_14 (and_14_out, Q0, not_29_out, Blt_B);
  and and_15 (and_15_out, not_11_out, not_12_out);
  not not_30 (not_30_out, Q0);
  and and_16 (and_16_out, not_30_out, Q1, ltC);
  not not_31 (not_31_out, Q1);
  and and_17 (and_17_out, Q0, not_31_out, Blt_C);
  and and_18 (and_18_out, not_13_out, not_14_out);
  not not_32 (not_32_out, Q0);
  and and_19 (and_19_out, not_32_out, Q1, ltD);
  not not_33 (not_33_out, Q1);
  and and_20 (and_20_out, Q0, not_33_out, Blt_C);
  and and_21 (and_21_out, not_15_out, not_16_out);
  not not_34 (not_34_out, Q0);
  and and_22 (and_22_out, not_34_out, Q1, ltD);
  not not_35 (not_35_out, Q1);
  and and_23 (and_23_out, Q0, not_35_out, Blt_D);
  and and_24 (and_24_out, not_17_out, not_18_out);
  not not_36 (not_36_out, Q0);
  and and_25 (and_25_out, not_36_out, Q1, Blt_E);
  and and_26 (and_26_out, Q0, not_37_out, Blt_D);
  not not_37 (not_37_out, Q1);
  and and_27 (and_27_out, not_19_out, not_20_out);
  not not_38 (not_38_out, Q0);
  and and_28 (and_28_out, not_38_out, Q1, Blt_E);
  or or_1 (en_0, and_1_out, and_2_out);
  or or_2 (en_1, and_3_out, and_4_out, and_5_out);
  or or_3 (en_2, and_6_out, and_7_out, and_8_out);
  or or_4 (en_3, and_9_out, and_10_out, and_11_out);
  or or_5 (en_4, and_12_out, and_13_out, and_14_out);
  or or_6 (en_5, and_15_out, and_16_out, and_17_out);
  or or_7 (en_6, and_18_out, and_19_out, and_20_out);
  or or_8 (en_7, and_21_out, and_22_out, and_23_out);
  or or_9 (en_8, and_24_out, and_25_out, and_26_out);
  or or_10 (en_9, and_27_out, and_28_out);
  not not_39 (not_39_out, Q0);
  not not_40 (not_40_out, Q1);
  not not_41 (not_41_out, Q0);
  not not_42 (not_42_out, Q1);
  not not_43 (not_43_out, Q0);
  not not_44 (not_44_out, Q1);
  not not_45 (not_45_out, Q0);
  not not_46 (not_46_out, Q1);
  not not_47 (not_47_out, Q0);
  not not_48 (not_48_out, Q0);
  not not_49 (not_49_out, Q0);
  not not_50 (not_50_out, Q1);
  and and_29 (finish_sorted, q_even, finish_odd);
  and and_30 (sel0_1, not_39_out, Q1, ltA);
  and and_31 (sel0_2, Q0, not_40_out, Blt_A);
  and and_32 (sel0_3, not_41_out, Q1, ltB);
  and and_33 (sel0_4, Q0, not_42_out, Blt_B);
  and and_34 (sel0_5, not_43_out, Q1, ltC);
  and and_35 (sel0_6, Q0, not_44_out, Blt_C);
  and and_36 (sel0_7, not_45_out, Q1, ltD);
  and and_37 (sel0_8, Q0, not_46_out, Blt_D);
  and and_38 (sel1_8, not_47_out, Q1, Blt_E);
  nand nand_1 (even, not_48_out, Q1);
  and and_39 (finish_odd, Q0, not_50_out, ~Blt_A, ~Blt_B, ~Blt_C, ~Blt_D);  // AND_Gate
  D_Flip_Flop d_ff_1 (.clk(clk), .D(in_even), .Q(q_even), .reset(rst));  // open: Qn, preset
  and and_40 (in_even, not_49_out, Q1, ~ltA, ~ltB, ~ltC, ~ltD, ~Blt_E);  // AND_Gate

  assign sel1_1 = sel0_2;
  assign sel1_2 = sel0_3;
  assign sel1_3 = sel0_4;
  assign sel1_4 = sel0_5;
  assign sel1_5 = sel0_6;
  assign sel1_6 = sel0_7;
  assign sel1_7 = sel0_8;
  assign sel_0 = sel0_1;
  assign sel_9 = sel1_8;
endmodule

module main (
  input  [15:0] v_0,
  input  [15:0] v_5,
  input  [15:0] v_1,
  input  [15:0] v_6,
  input  [15:0] v_2,
  input  [15:0] v_7,
  input  [15:0] v_3,
  input  [15:0] v_8,
  input  [15:0] v_4,
  input  [15:0] v_9
);

  wire clk_out, rst_out, sorted_1_sorted;
  wire [15:0] sorted_1_r_0, sorted_1_r_1, sorted_1_r_2, sorted_1_r_3, sorted_1_r_4, sorted_1_r_5,
       sorted_1_r_6, sorted_1_r_7, sorted_1_r_8, sorted_1_r_9;

  // Probe on v_0
  // Probe on v_1
  // Probe on v_2
  // Probe on v_3
  // Probe on v_4
  Clock clk (.out(clk_out));
  Button rst (.out(rst_out));
  // Probe on v_5
  // Probe on v_6
  // Probe on v_7
  // Probe on v_8
  // Probe on v_9
  Sorted sorted_1 (
    .v_0(v_0), .v_5(v_5), .v_1(v_1), .v_6(v_6), .v_2(v_2), .v_7(v_7), .v_3(v_3), .v_8(v_8), .v_4(v_4),
    .v_9(v_9), .sorted(sorted_1_sorted), .clk(clk_out), .rst(rst_out), .r_0(sorted_1_r_0),
    .r_5(sorted_1_r_5), .r_1(sorted_1_r_1), .r_6(sorted_1_r_6), .r_2(sorted_1_r_2), .r_7(sorted_1_r_7),
    .r_3(sorted_1_r_3), .r_8(sorted_1_r_8), .r_4(sorted_1_r_4), .r_9(sorted_1_r_9));
  // Probe on sorted_1_r_0
  // Probe on sorted_1_r_1
  // Probe on sorted_1_r_2
  // Probe on sorted_1_r_3
  // Probe on sorted_1_r_4
  // Probe on sorted_1_r_5
  // Probe on sorted_1_r_6
  // Probe on sorted_1_r_7
  // Probe on sorted_1_r_8
  // Probe on sorted_1_r_9
  LED sorted_2 (.in(sorted_1_sorted));

  // Notes on the sheet:
  //   Sort Vector of ten numbers
  //   Computer Engineering
  //   Luis Felipe de Deus
  //   Sorted Processor
endmodule

// SORTED
module Sorted (
  input  [15:0] v_0,
  input  [15:0] v_5,
  input  [15:0] v_1,
  input  [15:0] v_6,
  input  [15:0] v_2,
  input  [15:0] v_7,
  input  clk,
  input  [15:0] v_3,
  input  [15:0] v_8,
  input  rst,
  input  [15:0] v_4,
  input  [15:0] v_9,
  output sorted,
  output [15:0] r_0,
  output [15:0] r_5,
  output [15:0] r_1,
  output [15:0] r_6,
  output [15:0] r_2,
  output [15:0] r_7,
  output [15:0] r_3,
  output [15:0] r_8,
  output [15:0] r_4,
  output [15:0] r_9
);

  wire Blt_A, Blt_B, Blt_C, Blt_D, Blt_E, control_path_1_en_0, control_path_1_en_1, control_path_1_en_2,
       control_path_1_en_3, control_path_1_en_4, control_path_1_en_5, control_path_1_en_6,
       control_path_1_en_7, control_path_1_en_8, control_path_1_en_9, control_path_1_sel0_1,
       control_path_1_sel0_2, control_path_1_sel0_3, control_path_1_sel0_4, control_path_1_sel0_5,
       control_path_1_sel0_6, control_path_1_sel0_7, control_path_1_sel0_8, control_path_1_sel1_1,
       control_path_1_sel1_2, control_path_1_sel1_3, control_path_1_sel1_4, control_path_1_sel1_5,
       control_path_1_sel1_6, control_path_1_sel1_7, control_path_1_sel1_8, control_path_1_sel_0,
       control_path_1_sel_9, even, ltA, ltB, ltC, ltD, ltE;

  Control_Path control_path_1 (
    .clk(clk), .ltA(ltA), .rst(rst), .ltB(ltB), .ltC(ltC), .ltD(ltD), .ltE(ltE), .Blt_A(Blt_A),
    .Blt_B(Blt_B), .Blt_C(Blt_C), .Blt_D(Blt_D), .Blt_E(Blt_E), .sorted(sorted), .en_0(control_path_1_en_0),
    .en_1(control_path_1_en_1), .en_2(control_path_1_en_2), .en_3(control_path_1_en_3),
    .en_4(control_path_1_en_4), .en_5(control_path_1_en_5), .en_6(control_path_1_en_6),
    .en_7(control_path_1_en_7), .en_8(control_path_1_en_8), .en_9(control_path_1_en_9),
    .sel_0(control_path_1_sel_0), .sel0_1(control_path_1_sel0_1), .sel1_1(control_path_1_sel1_1),
    .sel0_2(control_path_1_sel0_2), .sel1_2(control_path_1_sel1_2), .sel0_3(control_path_1_sel0_3),
    .sel1_3(control_path_1_sel1_3), .sel0_4(control_path_1_sel0_4), .sel1_4(control_path_1_sel1_4),
    .sel0_5(control_path_1_sel0_5), .sel1_5(control_path_1_sel1_5), .sel0_6(control_path_1_sel0_6),
    .sel1_6(control_path_1_sel1_6), .sel0_7(control_path_1_sel0_7), .sel1_7(control_path_1_sel1_7),
    .sel0_8(control_path_1_sel0_8), .sel1_8(control_path_1_sel1_8), .sel_9(control_path_1_sel_9), .even(even));
  Data_Path data_path_1 (
    .v_0(v_0), .v_1(v_1), .v_2(v_2), .v_3(v_3), .v_4(v_4), .v_5(v_5), .v_6(v_6), .v_7(v_7), .v_8(v_8),
    .v_9(v_9), .clk(clk), .rst(rst), .lt_A(ltA), .BltA_A(Blt_A), .even(even), .en_1(control_path_1_en_1),
    .en_2(control_path_1_en_2), .en_3(control_path_1_en_3), .en_4(control_path_1_en_4),
    .en_5(control_path_1_en_5), .en_6(control_path_1_en_6), .en_7(control_path_1_en_7),
    .en_8(control_path_1_en_8), .en_9(control_path_1_en_9), .en_0(control_path_1_en_0), .lt_B(ltB),
    .lt_C(ltC), .lt_D(ltD), .lt_E(ltE), .BltA_B(Blt_B), .BltA_C(Blt_C), .BltA_D(Blt_D),
    .sel_0(control_path_1_sel_0), .sel1_1(control_path_1_sel0_1), .sel0_1(control_path_1_sel1_1),
    .sel1_2(control_path_1_sel0_2), .sel0_2(control_path_1_sel1_2), .sel1_3(control_path_1_sel0_3),
    .sel0_3(control_path_1_sel1_3), .sel1_4(control_path_1_sel0_4), .sel0_4(control_path_1_sel1_4),
    .sel1_5(control_path_1_sel0_5), .sel0_5(control_path_1_sel1_5), .sel1_6(control_path_1_sel0_6),
    .sel0_6(control_path_1_sel1_6), .sel1_7(control_path_1_sel0_7), .sel0_7(control_path_1_sel1_7),
    .sel1_8(control_path_1_sel0_8), .sel0_8(control_path_1_sel1_8), .sel_9(control_path_1_sel_9),
    .BltA_E(Blt_E), .reg_0(r_0), .reg_5(r_5), .reg_1(r_1), .reg_6(r_6), .reg_2(r_2), .reg_7(r_7), .reg3(r_3),
    .reg_8(r_8), .reg_4(r_4), .reg_9(r_9));
endmodule

module Debug (
);

  wire and_1_out, and_2_out, and_3_out, and_4_out, and_5_out, and_6_out, and_7_out, and_8_out, clk,
       clock_1_out, csu_1_out_5, csu_2_out_5, csu_3_out_5, csu_4_out_5, csu_5_out_5, csu_6_out_5,
       csu_7_out_5, csu_8_out_5, csu_9_out_5, rst, rst_out, save, undriven, undriven_2, undriven_3,
       undriven_4, undriven_5, undriven_6, undriven_7, undriven_8, undriven_9;
  wire [9:0] GERADOR_DE_ENTRADAS_q, register_11_q;
  wire [15:0] bit_extender_1_out, bit_extender_2_out, bit_extender_3_out, bit_extender_4_out,
       bit_extender_5_out, bit_extender_6_out, bit_extender_7_out, bit_extender_8_out, bit_extender_9_out,
       bit_extender_10_out, in0, in1, in2, in3, in4, in5, in6, in7, in8, in9, out0, out1, out2, out3, out4,
       out5, out6, out7, out8, out9;

  Clock clock_1 (.out(clock_1_out));
  Button u_rst (.out(rst_out));
  D_Flip_Flop d_ff_1 (.clk(clk), .D(save), .Q(rst));  // open: Qn, preset, reset
  Counter #(.width(10), .max('h3ff), .ongoal("stay")) GERADOR_DE_ENTRADAS (
    .count(save), .Q(GERADOR_DE_ENTRADAS_q), .clk(clock_1_out), .clr(rst_out));  // open: load, D, carry, preset, down
  assign bit_extender_1_out = {{15{1'b0}}, GERADOR_DE_ENTRADAS_q[0]};  // Bit_Extender bit_extender_1
  Register #(.width(16)) register_1 (.D(bit_extender_1_out), .Q(in0), .clk(clk), .clr(undriven));  // open: en
  assign bit_extender_2_out = {{15{1'b0}}, GERADOR_DE_ENTRADAS_q[1]};  // Bit_Extender bit_extender_2
  Register #(.width(16)) register_2 (
    .D(bit_extender_2_out), .Q(in1), .clk(clk), .clr(undriven_2), .preset(undriven));  // open: en, cs
  Register #(.width(16)) register_3 (
    .D(bit_extender_3_out), .Q(in2), .clk(clk), .clr(undriven_3), .preset(undriven_2));  // open: en, cs
  assign bit_extender_3_out = {{15{1'b0}}, GERADOR_DE_ENTRADAS_q[2]};  // Bit_Extender bit_extender_3
  Register #(.width(16)) register_4 (
    .D(bit_extender_4_out), .Q(in3), .clk(clk), .clr(undriven_4), .preset(undriven_3));  // open: en, cs
  assign bit_extender_4_out = {{15{1'b0}}, GERADOR_DE_ENTRADAS_q[3]};  // Bit_Extender bit_extender_4
  assign bit_extender_5_out = {{15{1'b0}}, GERADOR_DE_ENTRADAS_q[4]};  // Bit_Extender bit_extender_5
  Register #(.width(16)) register_5 (
    .D(bit_extender_5_out), .Q(in4), .clk(clk), .clr(undriven_5), .preset(undriven_4));  // open: en, cs
  Register #(.width(16)) register_6 (
    .D(bit_extender_6_out), .Q(in5), .clk(clk), .clr(undriven_6), .preset(undriven_5));  // open: en, cs
  assign bit_extender_6_out = {{15{1'b0}}, GERADOR_DE_ENTRADAS_q[5]};  // Bit_Extender bit_extender_6
  Register #(.width(16)) register_7 (
    .D(bit_extender_7_out), .Q(in6), .clk(clk), .clr(undriven_7), .preset(undriven_6));  // open: en, cs
  assign bit_extender_7_out = {{15{1'b0}}, GERADOR_DE_ENTRADAS_q[6]};  // Bit_Extender bit_extender_7
  Register #(.width(16)) register_8 (
    .D(bit_extender_8_out), .Q(in7), .clk(clk), .clr(undriven_8), .preset(undriven_7));  // open: en, cs
  assign bit_extender_8_out = {{15{1'b0}}, GERADOR_DE_ENTRADAS_q[7]};  // Bit_Extender bit_extender_8
  Register #(.width(16)) register_9 (
    .D(bit_extender_9_out), .Q(in8), .clk(clk), .clr(undriven_9), .preset(undriven_8));  // open: en, cs
  assign bit_extender_9_out = {{15{1'b0}}, GERADOR_DE_ENTRADAS_q[8]};  // Bit_Extender bit_extender_9
  Register #(.width(16)) register_10 (
    .D(bit_extender_10_out), .Q(in9), .clk(clk), .preset(undriven_9));  // open: en, clr, cs
  assign bit_extender_10_out = {{15{1'b0}}, GERADOR_DE_ENTRADAS_q[9]};  // Bit_Extender bit_extender_10
  Clock clock_2 (.out(clk));
  CSU csu_1 (.in_1(out0), .in_2(out1), .out_5(csu_1_out_5));  // open: out_3, out_4
  CSU csu_2 (.in_1(out1), .in_2(out2), .out_5(csu_2_out_5));  // open: out_3, out_4
  CSU csu_3 (.in_1(out2), .in_2(out3), .out_5(csu_3_out_5));  // open: out_3, out_4
  CSU csu_4 (.in_1(out3), .in_2(out4), .out_5(csu_4_out_5));  // open: out_3, out_4
  CSU csu_5 (.in_1(out4), .in_2(out5), .out_5(csu_5_out_5));  // open: out_3, out_4
  CSU csu_6 (.in_1(out5), .in_2(out6), .out_5(csu_6_out_5));  // open: out_3, out_4
  CSU csu_7 (.in_1(out6), .in_2(out7), .out_5(csu_7_out_5));  // open: out_3, out_4
  CSU csu_8 (.in_1(out7), .in_2(out8), .out_5(csu_8_out_5));  // open: out_3, out_4
  CSU csu_9 (.in_1(out8), .in_2(out9), .out_5(csu_9_out_5));  // open: out_3, out_4
  Sorted sorted_1 (
    .v_0(in0), .v_5(in5), .v_1(in1), .v_6(in6), .v_2(in2), .v_7(in7), .v_3(in3), .v_8(in8), .v_4(in4),
    .v_9(in9), .sorted(save), .clk(clk), .rst(rst), .r_0(out0), .r_5(out5), .r_1(out1), .r_6(out6),
    .r_2(out2), .r_7(out7), .r_3(out3), .r_8(out8), .r_4(out4), .r_9(out9));
  and and_1 (and_1_out, csu_1_out_5, csu_2_out_5);
  and and_2 (and_2_out, csu_3_out_5, csu_4_out_5);
  and and_3 (and_3_out, csu_5_out_5, csu_6_out_5);
  and and_4 (and_4_out, csu_7_out_5, csu_8_out_5);
  Register #(.width(10)) register_11 (.D(GERADOR_DE_ENTRADAS_q), .Q(register_11_q), .clk(clk));  // open: en, clr
  and and_5 (and_5_out, and_1_out, and_2_out);
  and and_6 (and_6_out, and_5_out, and_7_out);
  and and_7 (and_7_out, and_3_out, and_4_out);
  and and_8 (and_8_out, and_6_out, csu_9_out_5);
  RAM #(.addrWidth(10), .dataWidth(1), .Select("high")) ram_1 (
    .addr(register_11_q), .data(and_8_out), .sel(save), .clk(clk), .ld(1'b0));  // open: clr

  // Other names for the same wires on the sheet: sorted = save

  // Notes on the sheet:
  //   Nelson Roberto Weirich Junior
  //   e conte mais um no contador acima
  //   se necessário, faça uma lógica com o sinal de 'done' para que grave o sinal na memória
  //   entradas
  //   saídas
  //   menor elemento
  //   maior elemento
endmodule

module CSU (
  input  [15:0] in_1,
  input  [15:0] in_2,
  output [15:0] out_3,
  output [15:0] out_4,
  output out_5
);

  wire comparator_1_gt, comparator_1_lt;

  Comparator #(.width(16), .mode("unsigned")) comparator_1 (
    .a(in_1), .b(in_2), .gt(comparator_1_gt), .lt(comparator_1_lt));  // open: eq
  not not_1 (out_5, comparator_1_gt);
  Multiplexer #(.width(16), .enable("false")) multiplexer_1 (
    .in0(in_1), .in1(in_2), .out(out_3), .sel(comparator_1_gt));
  Multiplexer #(.width(16), .enable("false")) multiplexer_2 (
    .in0(in_1), .in1(in_2), .out(out_4), .sel(comparator_1_lt));
endmodule
