// Logisim project square_root_V2.circ as structural Verilog: 6 circuits, main circuit main
module Data_Path (
  input  [15:0] \input ,
  input  rst,
  input  sel_i0,
  input  en_ro_sq,
  input  clk,
  input  sel_i1,
  input  en_input,
  output less_than,
  output go_fw,
  output [7:0] root
);

  wire [7:0] adder_1_out, multiplexer_1_out;
  wire [8:0] r_s, root_9bits;
  wire [15:0] input_t, multiplexer_2_out, r_s_ext, square, square_ant;

  Adder adder_1 (.a(root), .b({8{1'b0}}), .out(adder_1_out), .cin(1'b1));  // open: cout
  Adder #(.width(16)) adder_2 (.a(square), .b(r_s_ext), .out(square_ant), .cin(1'b1));  // open: cout
  or or_1 (go_fw, \input [14], \input [15]);
  // Probe on {sel_i1, sel_i0}
  Comparator #(.width(16), .mode("unsigned")) comparator_1 (.a(input_t), .b(square), .lt(less_than));  // open: gt, eq
  Multiplexer #(.select(2), .width(8)) multiplexer_1 (
    .in0(8'h1), .in1(8'h80), .in2(adder_1_out), .in3({8{1'b0}}), .out(multiplexer_1_out),
    .sel({sel_i1, sel_i0}));  // open: en
  Register Reg_root (.D(multiplexer_1_out), .en(en_ro_sq), .Q(root), .clk(clk), .clr(rst));
  Multiplexer #(.select(2), .width(16)) multiplexer_2 (
    .in0(16'h4), .in1(16'h4101), .in2(square_ant), .in3({16{1'b0}}), .out(multiplexer_2_out),
    .sel({sel_i1, sel_i0}));  // open: en
  Shifter #(.width(9)) shifter_1 (.in(root_9bits), .\dist (4'b0001), .out(r_s));
  Register #(.width(16)) Reg_square (.D(multiplexer_2_out), .en(en_ro_sq), .Q(square), .clk(clk), .clr(rst));
  assign root_9bits = {{1{1'b0}}, root};  // Bit_Extender bit_extender_1
  assign r_s_ext = {{7{1'b0}}, r_s};  // Bit_Extender bit_extender_2
  Register #(.width(16)) Reg_input (.D(\input ), .en(en_input), .Q(input_t), .clk(clk), .clr(rst));

  // Other names for the same wires on the sheet: en_root = en_ro_sq; en_square = en_ro_sq; input_[15:0] = \input 
endmodule

module Control_Path (
  input  less_than,
  input  rst,
  input  go_fw,
  input  clk,
  output en_input,
  output en_ro_sq,
  output ready,
  output sel_i1,
  output sel_i0
);

  wire next_state_1_q0p, next_state_1_q1p, Q0p, Q1p;

  Next_State next_state_1 (
    .Q0(Q0p), .Q1(Q1p), .Q0p(next_state_1_q0p), .less_than(less_than), .rst(rst), .go_fw(go_fw),
    .Q1p(next_state_1_q1p));
  D_Flip_Flop #(.Pre_Clr_Positions("LEGACY"), .enable("true"), .NewFFLayout("false")) u_Q0p (
    .clk(clk), .D(next_state_1_q0p), .Q(Q0p), .en(1'b1), .reset(rst));  // open: Qn, preset
  D_Flip_Flop #(.Pre_Clr_Positions("LEGACY"), .enable("true"), .NewFFLayout("false")) u_Q1p (
    .clk(clk), .D(next_state_1_q1p), .Q(Q1p), .en(1'b1), .reset(rst));  // open: Qn, preset
  Output output_1 (
    .Q0(Q0p), .en_input(en_input), .Q1(Q1p), .en_ro_sq(en_ro_sq), .less_than(less_than), .ready(ready),
    .sel_i1(sel_i1), .sel_i0(sel_i0));

  // Other names for the same wires on the sheet: lt = less_than
endmodule

// NextState
module Next_State (
  input  Q0,
  input  Q1,
  input  less_than,
  input  rst,
  input  go_fw,
  output Q0p,
  output Q1p
);

  wire and_1_out, and_2_out, and_3_out, and_4_out, and_5_out, and_6_out, and_7_out, not_1_out, not_2_out,
       not_3_out, not_4_out, not_5_out, not_6_out, not_7_out, not_8_out, not_9_out, not_10_out;

  not not_1 (not_1_out, rst);
  not not_2 (not_2_out, go_fw);
  not not_3 (not_3_out, rst);
  not not_4 (not_4_out, rst);
  not not_5 (not_5_out, Q0);
  not not_6 (not_6_out, Q1);
  not not_7 (not_7_out, rst);
  not not_8 (not_8_out, rst);
  not not_9 (not_9_out, rst);
  not not_10 (not_10_out, rst);
  and and_1 (and_1_out, not_1_out, not_2_out);
  and and_2 (and_2_out, Q1, not_3_out);
  and and_3 (and_3_out, Q0, not_4_out);
  and and_4 (and_4_out, not_5_out, not_6_out, not_7_out, go_fw);
  and and_5 (and_5_out, Q1, less_than, not_8_out);
  and and_6 (and_6_out, Q0, less_than, not_9_out);
  and and_7 (and_7_out, Q0, Q1, not_10_out);
  or or_1 (Q0p, and_1_out, and_2_out, and_3_out);
  or or_2 (Q1p, and_4_out, and_5_out, and_6_out, and_7_out);
endmodule

module Output (
  input  Q0,
  input  Q1,
  input  less_than,
  output en_input,
  output en_ro_sq,
  output ready,
  output sel_i1,
  output sel_i0
);

  wire and_1_out, and_2_out, and_4_out, not_1_out, not_2_out, not_3_out, not_4_out, not_5_out;

  not not_1 (not_1_out, Q0);
  not not_2 (not_2_out, Q1);
  not not_3 (not_3_out, Q1);
  not not_4 (not_4_out, less_than);
  and and_1 (and_1_out, Q0, less_than);
  and and_2 (and_2_out, Q0, Q1);
  and and_3 (en_input, not_1_out, not_2_out);
  not not_5 (not_5_out, Q0);
  and and_4 (and_4_out, not_3_out, not_4_out);
  or or_1 (ready, and_1_out, and_2_out);
  or or_2 (en_ro_sq, not_5_out, and_4_out);

  assign sel_i0 = Q0;
  assign sel_i1 = Q1;
endmodule

module main (
  input  [15:0] INPUT,
  input  rst,
  output [7:0] ROOT,
  output ready
);

  wire clk_out;

  // Probe on INPUT
  SquareRoot SquareRoot (.rst(rst), .clk(clk_out), .\input (INPUT), .ready(ready), .root(ROOT));
  Clock clk (.out(clk_out));
  // Probe on ROOT

  // Notes on the sheet:
  //   SquareRoot Processor
  //   Computer Engineering
  //   Luis Felipe de Deus
endmodule

module SquareRoot (
  input  [15:0] \input ,
  input  rst,
  input  clk,
  output ready,
  output [7:0] root
);

  wire control_path_1_en_input, control_path_1_en_ro_sq, control_path_1_sel_i0, control_path_1_sel_i1, go_fw,
       less_than;

  Data_Path data_path_1 (
    .rst(rst), .en_ro_sq(control_path_1_en_ro_sq), .en_input(control_path_1_en_input),
    .sel_i0(control_path_1_sel_i1), .clk(clk), .less_than(less_than), .root(root), .\input (\input ),
    .sel_i1(control_path_1_sel_i0), .go_fw(go_fw));
  Control_Path control_path_1 (
    .sel_i0(control_path_1_sel_i0), .en_input(control_path_1_en_input), .less_than(less_than), .rst(rst),
    .clk(clk), .ready(ready), .sel_i1(control_path_1_sel_i1), .go_fw(go_fw),
    .en_ro_sq(control_path_1_en_ro_sq));
endmodule
